// Logisim project Trabajo_logisim.circ as structural Verilog
module Ejercicoo_1 (
  input  in_1,
  input  in_2,
  input  in_3,
  input  in_4,
  input  in_5,
  input  in_6,
  input  in_7,
  input  in_8,
  input  in_9,
  input  in_10,
  input  in_11,
  input  in_12,
  input  in_13,
  input  in_14,
  input  in_15,
  input  in_16,
  input  in_17,
  input  in_18,
  input  in_19,
  output out_20,
  output out_21,
  output out_22,
  output out_23,
  output out_24,
  output out_25,
  output out_26,
  output out_27,
  output out_28
);

  wire not_1_out, not_2_out, not_4_out, not_5_out, not_6_out, not_7_out;

  not not_1 (not_1_out, in_10);
  not not_2 (not_2_out, in_15);
  not NOT_3 (out_20, in_1);
  and AND (out_22, in_4, in_5);
  or NOR (out_23, in_6, in_7, not_1_out);
  and NAND (out_26, in_13, in_14, not_2_out);
  not not_4 (not_4_out, in_8);
  not not_5 (not_5_out, in_11);
  not not_6 (not_6_out, in_16);
  not not_7 (not_7_out, in_18);
  or XOR (out_24, not_4_out, not_5_out);
  or XNOR (out_27, not_6_out, not_7_out);
  or OR (out_21, in_2, in_3);
  xor XOR_2 (out_25, in_9, in_12);
  xnor XNOR_2 (out_28, in_17, in_19);
endmodule

module Not (
  input  in_1,
  output out_2
);

  Transistor #(.\type ("n")) transistor_1 (.in(1'b0), .out(out_2), .gate(in_1));
  Pull_Resistor #(.pull(1)) pull_resistor_1 (.node(out_2));
endmodule

module AND (
  input  in_1,
  input  in_2,
  output out_3
);

  wire transistor_1_out;

  Transistor #(.\type ("n")) transistor_1 (.in(1'b1), .out(transistor_1_out), .gate(in_1));
  Transistor #(.\type ("n")) transistor_2 (.in(transistor_1_out), .out(out_3), .gate(in_2));
  Pull_Resistor pull_resistor_1 (.node(out_3));
endmodule

module OR (
  input  in_1,
  input  in_2,
  output out_3
);

  Transistor #(.\type ("n")) transistor_1 (.in(1'b1), .out(out_3), .gate(in_1));
  Pull_Resistor pull_resistor_1 (.node(out_3));
  Transistor #(.\type ("n")) transistor_2 (.in(1'b1), .out(out_3), .gate(in_2));
endmodule
